# Fritzing sketch Garduino V2.0 (saved by Fritzing 0.9.1b)
circuit board: 6.41599cm x 5.43979cm
breadboards: 1

parts:
  NANO = Arduino Nano (Rev3.0)
  DHT-11 = female pin header, 3 pins [form="♀ (female)"]
  D9 = female pin header, 3 pins [form="♀ (female)"]
  Vin = female pin header, 2 pins [form="♀ (female)"]
  Soil = female pin header, 4 pins [form="♀ (female)"]
  Relays = female pin header, 4 pins [form="♀ (female)"]
  D8 = female pin header, 3 pins [form="♀ (female)"]
  A0 = female pin header, 3 pins [form="♀ (female)"]
  A1 = female pin header, 3 pins [form="♀ (female)"]
  A2 = female pin header, 3 pins [form="♀ (female)"]
  A6 = female pin header, 3 pins [form="♀ (female)"]
  A7 = female pin header, 3 pins [form="♀ (female)"]
  RTC = female pin header, 5 pins [form="♀ (female)"]
  Nokia_5110 = female pin header, 8 pins [form="♀ (female)"]

nets:
  N1: NANO.GND, DHT-11.pin3, D9.pin3, Vin.pin1, Soil.pin4, Relays.pin1, D8.pin3, A0.pin3, A1.pin3, A2.pin3, A6.pin3, A7.pin3, RTC.pin5, Nokia_5110.pin8
  N2: NANO.D2, DHT-11.pin2
  N3: NANO.D3, Nokia_5110.pin1
  N4: NANO.D4, Nokia_5110.pin2
  N5: NANO.D5, Nokia_5110.pin3
  N6: NANO.D6, Nokia_5110.pin4
  N7: NANO.D7, Nokia_5110.pin5
  N8: NANO.D8, D8.pin2
  N9: NANO.D9, D9.pin2
  N10: NANO.D10, Relays.pin3
  N11: NANO.D11/MOSI, Nokia_5110.pin7
  N12: NANO.D12/MISO, Relays.pin2
  N13: NANO.VIN, Vin.pin2
  N14: NANO.5V, DHT-11.pin1, D9.pin1, Soil.pin3, Relays.pin4, D8.pin1, A0.pin1, A1.pin1, A2.pin1, A6.pin1, A7.pin1, RTC.pin4
  N15: NANO.A7, A7.pin2
  N16: NANO.A6, A6.pin2
  N17: NANO.A5, RTC.pin2
  N18: NANO.A4, RTC.pin3
  N19: NANO.A3, Soil.pin1
  N20: NANO.A2, A2.pin2
  N21: NANO.A1, A1.pin2
  N22: NANO.A0, A0.pin2
  N23: NANO.3V3, Nokia_5110.pin6

notes:
  www.mkme.org
  V 1.0
  Urban Garden
